# Fritzing sketch TempHumLumSensor (saved by Fritzing 0.9.3b)
breadboards: 1

parts:
  AM1 = AM2302 Humidity and Temperature Sensor
  Part2 = Adafruit Feather 32u4 Adalogger [part_number="Adafruit #2795"]
  R1 = Resistor [tolerance=±5% resistance=10k package=THT]
  R2 = Resistor [tolerance=±5% resistance=27k package=THT]
  R3 = Photocell (LDR) [package=THT]
  Part1 = OLED Monochrome 128x64 0.96 inch [part_number=326]

nets:
  3.3V/Vcc: AM1.VDD, Part2.+3V3, R1.Pin_0, Part1.3.3V
  TEMP: AM1.DATA, Part2.5
  GND: AM1.GND, Part2.GND, R2.Pin_0, Part1.GND
  N1: Part2.A0, R2.Pin_1, R3.pin_1
  N2: Part2.13, Part1.MOSI_SDA
  N3: Part2.12, Part1.SCLK_SCK
  N4: Part2.11, Part1.DC_SA0
  CS: Part2.10, Part1.CS
  RST: Part2.9, Part1.RESET
  N5: R1.Pin_1, R3.pin_0

custom parts:
  Adafruit Feather 32u4 Adalogger: This is the Adafruit Feather 32u4 Adalogger - our take on an 'all-in-one' datalogger (or data-reader) with built in USB and battery charging. Its an Adafruit Feather 32u4 with a microSD holder ready to rock! We have other boards in the Feather family, check'em out here At the Feather 32u4's heart is at ATmega32u4 clocked at 8 MHz and at 3.3V logic, a chip setup we've had tons of experience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
  OLED Monochrome 128x64 0.96 inch: These displays are small, only about 1" diameter, but very readable due to the high contrast of an OLED display. This display is made of 128x64 individual white OLED pixels, each one is turned on or off by the controller chip. Because the display makes its own light, no backlight is required. This reduces the power required to run the OLED and is why the display has such high contrast; we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
